# Fritzing sketch 6507_memory_walk_final (saved by Fritzing 0.9.3b)
breadboards: 1

parts:
  CPU_-_6507 = IC, DIP package, 28 pins [chip_label=6507]
  R1 = Resistor [tolerance=±5% resistance=3k package=THT]
  R2 = Resistor [tolerance=±5% resistance=3k package=THT]
  S1-Reset = Momentary Switch [package=ksa_sealed_tac_switch]
  S2-RDY = Momentary Switch [package=ksa_sealed_tac_switch]
  C1 = Ceramic Capacitor [capacitance=100nF voltage=20V package="100 mil [THT, multilayer]"]
  Part1 = Arduino Uno (Rev3) - ICSP

nets:
  N1: CPU_-_6507.pin1, R1.Pin_0, S1-Reset.4
  N2: CPU_-_6507.pin2, C1.1
  N3: CPU_-_6507.pin3, R2.Pin_0, S2-RDY.4
  N4: CPU_-_6507.pin4, R1.Pin_1, R2.Pin_1, C1.0
  N5: CPU_-_6507.pin5, Part1.D2
  N6: CPU_-_6507.pin6, Part1.D3_PWM
  N7: CPU_-_6507.pin7, Part1.D4
  N8: CPU_-_6507.pin8, Part1.D5_PWM
  N9: CPU_-_6507.pin9, Part1.D6_PWM
  N10: CPU_-_6507.pin10, Part1.D7
  N11: CPU_-_6507.pin11, Part1.D8
  N12: CPU_-_6507.pin12, Part1.D9_PWM
  N13: CPU_-_6507.pin13, Part1.D10_PWM/SS
  N14: CPU_-_6507.pin14, Part1.D11_PWM/MOSI
  N15: CPU_-_6507.pin15, Part1.D12/MISO
  N16: CPU_-_6507.pin16, Part1.D13/SCK
  N17: CPU_-_6507.pin17, Part1.A0
  N18: CPU_-_6507.pin18, CPU_-_6507.pin19, CPU_-_6507.pin20, CPU_-_6507.pin22, CPU_-_6507.pin24
  N19: CPU_-_6507.pin21, CPU_-_6507.pin23, CPU_-_6507.pin25, S1-Reset.1, S2-RDY.1
  N20: CPU_-_6507.pin27, Part1.A5/SCL

notes:
  NOP = 0xEA = 11101010
  (from right to left)
