# Fritzing sketch 6507_and_cart_connector (saved by Fritzing 0.9.3b)
breadboards: 1

parts:
  CPU_-_6507 = IC, DIP package, 28 pins [chip_label=6507]
  R1 = Resistor [tolerance=±5% resistance=3k package=THT]
  R2 = Resistor [tolerance=±5% resistance=3k package=THT]
  S1-Reset = Momentary Switch [package=ksa_sealed_tac_switch]
  S2-RDY = Momentary Switch [package=ksa_sealed_tac_switch]
  C1 = Ceramic Capacitor [capacitance=100nF voltage=20V package="100 mil [THT, multilayer]"]
  Part1 = Arduino Uno (Rev3) - ICSP
  J2 = shrouded pin header, 24 pins [form="♂ (shrouded male)"]

nets:
  N1: CPU_-_6507.pin1, CPU_-_6507.pin3, R1.Pin_0, R2.Pin_0, S1-Reset.2
  N2: CPU_-_6507.pin2, C1.0, J2.pin12, J2.pin24
  N3: CPU_-_6507.pin4, R1.Pin_1, R2.Pin_1, C1.1, J2.pin23
  N4: CPU_-_6507.pin5, Part1.D0/RX, J2.pin8
  N5: CPU_-_6507.pin6, Part1.D1/TX, J2.pin7
  N6: CPU_-_6507.pin7, Part1.D2, J2.pin6
  N7: CPU_-_6507.pin8, Part1.D3_PWM, J2.pin5
  N8: CPU_-_6507.pin9, Part1.D4, J2.pin4
  N9: CPU_-_6507.pin10, Part1.D5_PWM, J2.pin3
  N10: CPU_-_6507.pin11, Part1.D6_PWM, J2.pin2
  N11: CPU_-_6507.pin12, Part1.D7, J2.pin1
  N12: CPU_-_6507.pin13, Part1.D8, J2.pin22
  N13: CPU_-_6507.pin14, Part1.D9_PWM, J2.pin21
  N14: CPU_-_6507.pin15, Part1.D10_PWM/SS, J2.pin19
  N15: CPU_-_6507.pin16, Part1.D11_PWM/MOSI, J2.pin20
  N16: CPU_-_6507.pin17, Part1.D12/MISO, J2.pin18
  N17: CPU_-_6507.pin18, J2.pin17
  N18: CPU_-_6507.pin19, J2.pin16
  N19: CPU_-_6507.pin20, J2.pin15
  N20: CPU_-_6507.pin21, J2.pin14
  N21: CPU_-_6507.pin22, J2.pin13
  N22: CPU_-_6507.pin23, J2.pin11
  N23: CPU_-_6507.pin24, J2.pin10
  N24: CPU_-_6507.pin25, J2.pin9
  N25: CPU_-_6507.pin27, Part1.D13/SCK
  N26: S1-Reset.1, S2-RDY.3
