# Fritzing sketch 6507-and-cart (saved by Fritzing 0.9.3b)
breadboards: 1

parts:
  CPU_-_6507 = IC, DIP package, 28 pins [chip_label=6507]
  R1 = Resistor [tolerance=±5% resistance=3k package=THT]
  R2 = Resistor [tolerance=±5% resistance=3k package=THT]
  S1-Reset = Momentary Switch [package=ksa_sealed_tac_switch]
  S2-RDY = Momentary Switch [package=ksa_sealed_tac_switch]
  C1 = Ceramic Capacitor [capacitance=100nF voltage=20V package="100 mil [THT, multilayer]"]
  Part1 = Arduino Uno (Rev3) - ICSP
  CART = Atari 2600 Cart Connector

nets:
  N1: CPU_-_6507.pin1, R1.Pin_0, S1-Reset.4
  N2: CPU_-_6507.pin2, S1-Reset.1, S2-RDY.1, C1.1, Part1.GND, CART.pin12_-_GND, CART.pin24_-_SGND
  N3: CPU_-_6507.pin3, R2.Pin_0, S2-RDY.4
  N4: CPU_-_6507.pin4, R1.Pin_1, R2.Pin_1, C1.0, Part1.5V, CART.pin23_-_+5V
  N5: CPU_-_6507.pin5, CART.pin8_-_A0
  N6: CPU_-_6507.pin6, CART.pin7_-_A1
  N7: CPU_-_6507.pin7, CART.pin6_-_A2
  N8: CPU_-_6507.pin8, CART.pin5_-_A3
  N9: CPU_-_6507.pin9, CART.pin4_-_A4
  N10: CPU_-_6507.pin10, CART.pin3_-_A5
  N11: CPU_-_6507.pin11, CART.pin2_-_A6
  N12: CPU_-_6507.pin12, CART.pin1_-_A7
  N13: CPU_-_6507.pin13, CART.pin22_-_A8
  N14: CPU_-_6507.pin14, CART.pin21_-_A9
  N15: CPU_-_6507.pin15, CART.pin19_-_A10
  N16: CPU_-_6507.pin16, CART.pin20_-_A11
  N17: CPU_-_6507.pin17, CART.pin18_-_A12
  N18: CPU_-_6507.pin18, Part1.D9_PWM, CART.pin17_-_D8
  N19: CPU_-_6507.pin19, Part1.D8, CART.pin16_-_D7
  N20: CPU_-_6507.pin20, Part1.D7, CART.pin15_-_D6
  N21: CPU_-_6507.pin21, Part1.D6_PWM, CART.pin14_-_D5
  N22: CPU_-_6507.pin22, Part1.D5_PWM, CART.pin13_-_D4
  N23: CPU_-_6507.pin23, Part1.D4, CART.pin11_-_D3
  N24: CPU_-_6507.pin24, Part1.D3_PWM, CART.pin10_-_D2
  N25: CPU_-_6507.pin25, Part1.D2, CART.pin9_-_D1
  N26: CPU_-_6507.pin27, Part1.A5/SCL

custom parts:
  Atari 2600 Cart Connector: Atari 2600 VCS Cart Connector A regular 24-pin edge connector seen from the oustide of the console Pins named according to Atari 2600 schematics in https://atariage.com/2600/archives/schematics/index.html
