# Fritzing sketch ring-detection (saved by Fritzing 0.9.8b)
perfboards: 1

parts:
  D1 = Zener Diode [part_number=1N4007 breakdown_voltage=3.6V package="300 mil [THT]"]
  U1 = Optocoupler [package=THT]
  C1 = Electrolytic Capacitor [capacitance=10μF voltage=35V package="0605 [SMD, electrolytic]"]
  R1 = Resistor [tolerance=±5% resistance=1000 package="0402 [SMD]"]
  12V_IN_(+) = Header 1 [package=1x01_offset]
  12V_AC_IN_(-) = Header 1 [package=1x01_offset]
  ESP_GND = Header 1 [package=1x01_offset]
  ESP_D4 = Header 1 [package=1x01_offset]

nets:
  N1: D1.cathode, C1.+, R1.Pin_0
  N2: D1.anode, 12V_IN_(+).1
  N3: U1.Pin_1, R1.Pin_1
  N4: U1.Pin_2, C1.-, 12V_AC_IN_(-).1
  N5: U1.Pin_4, ESP_GND.1
  N6: U1.Pin_5, ESP_D4.1
